// Logisim project cpu.circ as structural Verilog: 2 circuits, main circuit CPU
module CPU (
  input  [31:0] Instruction,
  input  CLK,
  output [31:0] s0,
  output [31:0] s1,
  output [31:0] t0,
  output [31:0] t1,
  output [31:0] a0,
  output [31:0] ra,
  output [31:0] sp,
  output [31:0] PC
);

  wire pc_1_p1;
  wire [31:0] alu_1_out, brcomp_1_p1, incrementer_1_p1, incrementer_1_p2, incrementer_1_p3, main_1_p1,
       main_1_p3, multiplexer_2_out, multiplexer_3_out, regfile_1_p1;

  // Incrementer incrementer_1: pin names not known; wires that end beside it: incrementer_1_p1, incrementer_1_p2, incrementer_1_p3
  Multiplexer #(.width(32)) multiplexer_1 (
    .in0(incrementer_1_p2), .in1(main_1_p1), .out(incrementer_1_p3));  // open: sel, en
  // PC pc_1: pin names not known; wires that end beside it: pc_1_p1, pc_1_p1, incrementer_1_p1
  // RegFile regfile_1: pin names not known; wires that end beside it: regfile_1_p1, incrementer_1_p1
  Multiplexer #(.width(32)) multiplexer_2 (
    .in0(incrementer_1_p1), .in1(regfile_1_p1), .out(multiplexer_2_out));  // open: sel, en
  // Brcomp brcomp_1: pin names not known; wires that end beside it: brcomp_1_p1, regfile_1_p1, brcomp_1_p1
  Multiplexer #(.width(32)) multiplexer_3 (.in0(brcomp_1_p1), .out(multiplexer_3_out));  // open: in1, sel, en
  ALU alu_1 (.A(multiplexer_2_out), .B(multiplexer_3_out), .Out(alu_1_out));  // open: ALU_Op
  // memory_main main_1: pin names not known; wires that end beside it: main_1_p1, brcomp_1_p1, main_1_p3
  Multiplexer #(.select(2), .width(32)) multiplexer_4 (
    .in0(incrementer_1_p2), .in1(alu_1_out), .in2(main_1_p3));  // open: in3, out, sel, en

  // Other names for the same wires on the sheet: fetch_addr[31:0] = PC; INST[31:0] = Instruction

  // Notes on the sheet:
  //   NOTE
  //   Please do not modify/replace/move/change/delete/etc input and output pins
  //   These are debug/test outputs from your circuit
endmodule

module Brcomp (
  input  [31:0] in_1,
  input  [31:0] in_2,
  input  [31:0] in_3,
  input  [31:0] in_4,
  output [31:0] out_5
);

  wire comparator_1_eq, comparator_1_gt, comparator_1_lt;
  wire [31:0] bit_extender_1_out, bit_extender_2_out, bit_extender_3_out, multiplexer_1_out,
       multiplexer_2_out, multiplexer_3_out, not_1_out;

  Comparator #(.width(32)) comparator_1 (
    .a(in_2), .b(in_3), .gt(comparator_1_gt), .eq(comparator_1_eq), .lt(comparator_1_lt));
  Bit_Extender #(.in_width(1), .out_width(32)) bit_extender_1 (.out(bit_extender_1_out));  // open: in
  assign bit_extender_2_out = {{31{1'b0}}, comparator_1_lt};  // Bit_Extender bit_extender_2
  assign bit_extender_3_out = {{31{1'b0}}, comparator_1_eq};  // Bit_Extender bit_extender_3
  Multiplexer #(.width(32)) multiplexer_1 (
    .in0(bit_extender_1_out), .in1(bit_extender_2_out), .out(multiplexer_1_out));  // open: sel, en
  Multiplexer #(.width(32)) multiplexer_2 (
    .in0(multiplexer_1_out), .in1(bit_extender_3_out), .out(multiplexer_2_out));  // open: sel, en
  Multiplexer #(.width(32)) multiplexer_3 (
    .in0(multiplexer_2_out), .in1(not_1_out), .out(multiplexer_3_out));  // open: sel, en
  assign not_1_out = ~multiplexer_2_out;  // NOT_Gate not_1, 32 bits wide
  Multiplexer #(.select(2), .width(32)) multiplexer_4 (
    .in0(in_1), .in1(in_1), .in2(multiplexer_3_out), .in3(in_1), .out(out_5), .sel({in_4[6], in_4[2]}));  // open: en
endmodule
